# Fritzing sketch dioderctrl (saved by Fritzing 0.9.0b)
breadboards: 1

parts:
  Bauteil1 = Spark Core (v1.0)
  IC2 = ULN2003A [package="SO16 [SMD]"]
  J1 = female pin header, 4 pins [form="♀ (female)"]
  J2 = female pin header, 4 pins [form="♀ (female)"]

nets:
  N1: Bauteil1.A5, IC2.Out_6
  N2: Bauteil1.A6, IC2.Out_7
  N3: Bauteil1.A7, IC2.COM_-_Common
  N4: Bauteil1.GND, IC2.Out_1, J2.pin1
  N5: IC2.In_6, J1.pin2
  N6: IC2.In_7, J1.pin3
  N7: IC2.0V, J1.pin4

notes:
  DIODER Connector
  DIODER Power supply
